# Fritzing sketch circuit (saved by Fritzing 0.9.0b)
breadboards: 1

parts:
  U1 = Spark Core (v1.0)
  Left = Basic Servo
  Right = Basic Servo
  VCC1 = 4 x AAA Battery Mount

nets:
  GND: U1.GND, Left.gnd, Right.gnd, VCC1.-
  VCC: Left.vcc, Right.vcc, VCC1.+

custom parts:
  Spark Core (v1.0): The Spark Core is a tiny Wi-Fi development board that makes it easy to create internet-connected hardware. The Core is all you need to get started; power it over USB and in minutes you'll be controlling LEDs, switches and motors and collecting data from sensors over the internet! It has 8 digital I/O pins, 8 analog I/O pins, 8 PWM pins; UART (Serial), SPI, I2C, and JTAG peripherals available.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
